# Fritzing sketch LegoEsp32SunTracker (saved by Fritzing 0.9.10b)
circuit board: 8.46667cm x 5.64444cm
breadboards: 1

parts:
  U1 = ESP32S-HiLetgo [part_number=ESP32S-HiLetgo]
  Top_right = PHOTOCELL [package=photocell-kit]
  Bottom_right = PHOTOCELL [package=photocell-kit]
  Bottom_left = PHOTOCELL [package=photocell-kit]
  Top_left = PHOTOCELL [package=photocell-kit]
  R21 = Resistor [tolerance=±5% resistance=10k power=0.25 package=THT]
  R22 = Resistor [tolerance=±5% resistance=10k power=0.25 package=THT]
  R23 = Resistor [tolerance=±5% resistance=10k power=0.25 package=THT]
  R24 = Resistor [tolerance=±5% resistance=10k power=0.25 package=THT]
  Azimuth = Dagu DGServo 9g (Top view) [part_number=RS001B]
  Altitude = Dagu DGServo 9g (Top view) [part_number=RS001B]

nets:
  Top left: U1.GPIO36, Top_left.P$1, R23.Pin_1
  Bottom left: U1.GPIO39, Bottom_left.P$1, R22.Pin_1
  Bottom right: U1.GPIO34, Bottom_right.P$2, R21.Pin_0
  Top right: U1.GPIO35, Top_right.P$2, R24.Pin_0
  GND: U1.GND, R21.Pin_1, R22.Pin_0, R23.Pin_0, R24.Pin_1, Azimuth.gnd, Altitude.gnd
  5V: U1.VIN, Top_right.P$1, Bottom_right.P$1, Bottom_left.P$2, Top_left.P$2, Azimuth.vcc, Altitude.vcc
  N1: U1.GPIO22, Azimuth.pulse
  N2: U1.GPIO23, Altitude.pulse

custom parts:
  ESP32S-HiLetgo: HiLetgo ESP-WROOM-32 ESP32 ESP-32S Development Board 2.4GHz Dual-Mode WiFi + Bluetooth Dual Cores Microcontroller The ESP32 integrated with Antenna switches, RF Balun, power amplifiers, low-noise amplifiers, filters, and management modules, and the entire solution occupies the least area of PCB. 2.4 GHz Wi-Fi plus Bluetooth dual-mode chip, with TSMC Ultra-low power consumption 40nm technology,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
